// Logisim project alu.circ as structural Verilog: 1 circuit, main circuit alu
module alu (
  input  [31:0] A,
  input  [31:0] B,
  input  [3:0] ALUSel,
  output [31:0] Result
);

  wire comparator_1_lt;
  wire [31:0] add0, AND1, MUL10, MULH14, MULHU11, multiplexer_1_out, multiplexer_2_out, multiplexer_4_out,
       multiplexer_6_out, multiplexer_7_out, multiplexer_8_out, OR2, SLL6, SLT7, SRA5, SRL4, sub12, XOR3;

  Adder #(.width(32)) adder_1 (.a(A), .b(B), .out(add0));  // open: cin, cout
  assign AND1 = A & B;  // AND_Gate and_1, 32 bits wide
  Multiplier #(.mode("twosComplement"), .width(32)) multiplier_1 (
    .a(A), .b(B), .out(MUL10), .cout(MULH14));  // open: cin
  assign OR2 = A | B;  // OR_Gate or_1, 32 bits wide
  assign XOR3 = A ^ B;  // XOR_Gate xor_1, 32 bits wide
  Multiplier #(.width(32)) multiplier_2 (.a(A), .b(B), .cout(MULHU11));  // open: out, cin
  Multiplexer #(.enable("false"), .select(2), .width(32)) multiplexer_1 (
    .in0(add0), .in1(AND1), .in2(OR2), .in3(XOR3), .out(multiplexer_1_out), .sel(ALUSel[1:0]));
  Shifter #(.shift("lr"), .width(32)) shifter_1 (.in(A), .\dist (B[4:0]), .out(SRL4));
  Shifter #(.shift("ar"), .width(32)) shifter_2 (.in(A), .\dist (B[4:0]), .out(SRA5));
  Shifter #(.width(32)) shifter_3 (.in(A), .\dist (B[4:0]), .out(SLL6));
  Comparator #(.width(32)) comparator_1 (.a(A), .b(B), .lt(comparator_1_lt));  // open: gt, eq
  Multiplexer #(.enable("false"), .width(32)) multiplexer_2 (
    .in0(multiplexer_1_out), .in1(multiplexer_4_out), .out(multiplexer_2_out), .sel(ALUSel[2]));
  Multiplexer #(.enable("false"), .width(32)) multiplexer_3 (
    .in0({32{1'b0}}), .in1(32'h1), .out(SLT7), .sel(comparator_1_lt));
  Subtractor #(.width(32)) subtractor_1 (.a(A), .b(B), .out(sub12));  // open: bin, bout
  Multiplexer #(.enable("false"), .select(2), .width(32)) multiplexer_4 (
    .in0(SRL4), .in1(SRA5), .in2(SLL6), .in3(SLT7), .out(multiplexer_4_out), .sel(ALUSel[1:0]));
  Multiplexer #(.enable("false"), .width(32)) multiplexer_5 (
    .in0(multiplexer_2_out), .in1(multiplexer_6_out), .out(Result), .sel(ALUSel[3]));
  Multiplexer #(.enable("false"), .width(32)) multiplexer_6 (
    .in0(multiplexer_7_out), .in1(multiplexer_8_out), .out(multiplexer_6_out), .sel(ALUSel[2]));
  Multiplexer #(.enable("false"), .select(2), .width(32)) multiplexer_7 (
    .in2(MUL10), .in3(MULHU11), .out(multiplexer_7_out), .sel(ALUSel[1:0]));  // open: in0, in1
  Multiplexer #(.enable("false"), .select(2), .width(32)) multiplexer_8 (
    .in0(sub12), .in1(B), .in2(MULH14), .out(multiplexer_8_out), .sel(ALUSel[1:0]));  // open: in3

  // Other names for the same wires on the sheet: ALUSel01[1:0] = ALUSel[1:0]

  // Notes on the sheet:
  //   INPUTS to your circuit
  //   DON'T CHANGE THE LOCATIONS OF THE INPUTS AND OUTPUTS!
  //   OUTPUT from your circuit
endmodule
