// Logisim project control_logic.circ as structural Verilog: 1 circuit, main circuit control_logic
module control_logic (
  input  [31:0] inst,
  input  BrEq,
  input  BrLt,
  output PCSel,
  output RegWEn,
  output [2:0] ImmSel,
  output BrUn,
  output ASel,
  output BSel,
  output [3:0] ALUSel,
  output MemRW,
  output [1:0] WBSel,
  output CSRSel,
  output CSRWen
);

  wire and_13_out, and_17_out, and_18_out, and_19_out, and_20_out, and_21_out, and_22_out, and_23_out,
       and_24_out, and_25_out, and_26_out, and_27_out, and_28_out, B_Type, blt, bltu, decoder_1_out0,
       decoder_1_out1, decoder_1_out2, decoder_1_out3, decoder_1_out4, decoder_1_out5, decoder_1_out6,
       decoder_1_out7, HEX00, HEX01, HEX20, I_Type1, I_Type2, I_Type3, I_Type4, multiplexer_1_out, not_1_out,
       not_2_out, not_3_out, not_4_out, not_5_out, not_6_out, not_7_out, not_8_out, not_9_out, not_10_out,
       not_11_out, not_12_out, not_13_out, not_14_out, not_15_out, not_16_out, not_17_out, not_18_out,
       not_19_out, not_20_out, not_21_out, not_22_out, not_23_out, not_24_out, not_25_out, not_26_out,
       not_27_out, not_28_out, not_29_out, not_30_out, not_32_out, not_33_out, not_34_out, not_35_out,
       not_37_out, not_38_out, not_39_out, not_40_out, not_41_out, not_42_out, not_43_out, not_44_out,
       not_45_out, not_46_out, not_47_out, not_48_out, not_49_out, not_50_out, or_1_out, or_2_out, or_4_out,
       or_5_out, or_6_out, or_8_out, or_9_out, R_Type, S_Type, U_Type1, U_Type2, UJ_Type;

  not not_1 (not_1_out, inst[12]);
  and and_1 (BrUn, not_1_out, inst[13], inst[14]);
  not not_2 (not_2_out, inst[2]);
  not not_3 (not_3_out, inst[3]);
  not not_4 (not_4_out, inst[6]);
  not not_5 (not_5_out, inst[2]);
  not not_6 (not_6_out, inst[3]);
  not not_7 (not_7_out, inst[4]);
  not not_8 (not_8_out, inst[2]);
  not not_9 (not_9_out, inst[3]);
  not not_10 (not_10_out, inst[4]);
  not not_11 (not_11_out, inst[6]);
  not not_12 (not_12_out, inst[2]);
  not not_13 (not_13_out, inst[3]);
  not not_14 (not_14_out, inst[4]);
  not not_15 (not_15_out, inst[5]);
  not not_16 (not_16_out, inst[6]);
  not not_17 (not_17_out, inst[2]);
  not not_18 (not_18_out, inst[3]);
  not not_19 (not_19_out, inst[5]);
  not not_20 (not_20_out, inst[6]);
  not not_21 (not_21_out, inst[3]);
  not not_22 (not_22_out, inst[4]);
  not not_23 (not_23_out, inst[2]);
  not not_24 (not_24_out, inst[3]);
  not not_25 (not_25_out, inst[4]);
  not not_26 (not_26_out, inst[3]);
  not not_27 (not_27_out, inst[5]);
  not not_28 (not_28_out, inst[6]);
  not not_29 (not_29_out, inst[3]);
  not not_30 (not_30_out, inst[6]);
  and and_2 (R_Type, inst[0], inst[1], not_2_out, not_3_out, inst[4], inst[5], not_4_out);
  and and_3 (B_Type, inst[0], inst[1], not_5_out, not_6_out, not_7_out, inst[5], inst[6]);
  and and_4 (S_Type, inst[0], inst[1], not_8_out, not_9_out, not_10_out, inst[5], not_11_out);
  and and_5 (I_Type1, inst[0], inst[1], not_12_out, not_13_out, not_14_out, not_15_out, not_16_out);
  and and_6 (I_Type2, inst[0], inst[1], not_17_out, not_18_out, inst[4], not_19_out, not_20_out);
  and and_7 (I_Type3, inst[0], inst[1], inst[2], not_21_out, not_22_out, inst[5], inst[6]);
  and and_8 (I_Type4, inst[0], inst[1], not_23_out, not_24_out, inst[4], inst[5], inst[6]);
  and and_9 (UJ_Type, inst[0], inst[1], inst[2], inst[3], not_25_out, inst[5], inst[6]);
  and and_10 (U_Type1, inst[0], inst[1], inst[2], not_26_out, inst[4], not_27_out, not_28_out);
  and and_11 (U_Type2, inst[0], inst[1], inst[2], not_29_out, inst[4], inst[5], not_30_out);
  not not_31 (BSel, R_Type);
  not not_32 (not_32_out, inst[2]);
  not not_33 (not_33_out, inst[3]);
  not not_34 (not_34_out, inst[4]);
  not not_35 (not_35_out, inst[6]);
  and and_12 (MemRW, inst[0], inst[1], not_32_out, not_33_out, not_34_out, inst[5], not_35_out);
  or or_1 (or_1_out, R_Type, I_Type1, I_Type3, I_Type2, S_Type);
  not not_36 (ASel, or_1_out);
  or or_2 (or_2_out, inst[7], inst[8], inst[9], inst[10], inst[11]);
  nor nor_1 (WBSel[0], I_Type3, UJ_Type, I_Type1);
  or or_3 (WBSel[1], I_Type3, UJ_Type);
  or or_4 (or_4_out, UJ_Type, R_Type, I_Type1, I_Type3, I_Type2, U_Type1, U_Type2);
  or or_5 (or_5_out, I_Type1, I_Type2, I_Type3);
  or or_6 (or_6_out, U_Type1, U_Type2);
  and and_13 (and_13_out, I_Type4, inst[14]);
  and and_14 (RegWEn, or_2_out, or_4_out);
  Priority_Encoder priority_encoder_1 (
    .in0(or_5_out), .in1(S_Type), .in2(B_Type), .in3(UJ_Type), .in4(or_6_out), .in5(and_13_out), .out(ImmSel));  // open: in6, in7, en_in, gs, en_out
  not not_37 (not_37_out, inst[2]);
  not not_38 (not_38_out, inst[3]);
  not not_39 (not_39_out, inst[4]);
  not not_40 (not_40_out, BrUn);
  and and_15 (bltu, BrLt, BrUn);
  and and_16 (blt, BrLt, not_40_out);
  not not_41 (not_41_out, inst[4]);
  not not_42 (not_42_out, inst[3]);
  not not_43 (not_43_out, inst[4]);
  and and_17 (and_17_out, inst[0], inst[1], not_37_out, not_38_out, not_39_out, inst[5], inst[6]);
  and and_18 (and_18_out, inst[0], inst[1], inst[2], inst[3], not_41_out, inst[5], inst[6]);
  and and_19 (and_19_out, inst[0], inst[1], inst[2], not_42_out, not_43_out, inst[5], inst[6]);
  not not_44 (not_44_out, BrEq);
  not not_45 (not_45_out, blt);
  not not_46 (not_46_out, bltu);
  Multiplexer #(.select(3)) multiplexer_1 (
    .in0(BrEq), .in1(not_44_out), .in4(blt), .in5(not_45_out), .in6(bltu), .in7(not_46_out),
    .out(multiplexer_1_out), .sel(inst[14:12]), .en(and_17_out));  // open: in2, in3
  or or_7 (PCSel, multiplexer_1_out, and_18_out, and_19_out);
  not not_47 (not_47_out, inst[25]);
  not not_48 (not_48_out, inst[30]);
  nor nor_2 (HEX00, inst[25], inst[26], inst[27], inst[28], inst[29], inst[30], inst[31]);
  nor nor_3 (HEX01, not_47_out, inst[26], inst[27], inst[28], inst[29], inst[30], inst[31]);
  nor nor_4 (HEX20, inst[25], inst[26], inst[27], inst[28], inst[29], not_48_out, inst[31]);
  or or_8 (or_8_out, R_Type, I_Type2);
  not not_49 (not_49_out, R_Type);
  not not_50 (not_50_out, I_Type2);
  and and_20 (and_20_out, I_Type2, decoder_1_out0);
  Decoder #(.select(3)) decoder_1 (
    .out0(decoder_1_out0), .out1(decoder_1_out1), .out2(decoder_1_out2), .out3(decoder_1_out3),
    .out4(decoder_1_out4), .out5(decoder_1_out5), .out6(decoder_1_out6), .out7(decoder_1_out7),
    .sel(inst[14:12]), .en(or_8_out));
  and and_21 (and_21_out, not_49_out, not_50_out);
  and and_22 (and_22_out, decoder_1_out0, R_Type, HEX00);
  or or_9 (or_9_out, and_21_out, and_20_out, and_22_out);
  and and_23 (and_23_out, decoder_1_out0, R_Type, HEX01);
  and and_24 (and_24_out, decoder_1_out5, HEX00);
  and and_25 (and_25_out, decoder_1_out5, HEX20);
  Priority_Encoder #(.select(4)) priority_encoder_2 (
    .in0(or_9_out), .in1(decoder_1_out7), .in2(decoder_1_out6), .in3(decoder_1_out4), .in4(and_24_out),
    .in5(and_25_out), .in6(and_27_out), .in7(decoder_1_out2), .in10(and_23_out), .in11(decoder_1_out3),
    .in12(and_26_out), .in13(U_Type2), .in14(and_28_out), .out(ALUSel));  // open: in8, in9, in15
  and and_26 (and_26_out, decoder_1_out0, R_Type, HEX20);
  and and_27 (and_27_out, decoder_1_out1, R_Type, HEX00);
  and and_28 (and_28_out, decoder_1_out1, R_Type, HEX01);

  // Other names for the same wires on the sheet: opcode[6:0] = inst[6:0]; rd[4:0] = inst[11:7];
  //   funct3[2:0] = inst[14:12]; rs1[4:0] = inst[19:15]; rs2[4:0] = inst[24:20]; funct7[6:0] = inst[31:25]

  // Notes on the sheet:
  //   INPUTS to your circuit
  //   The tunnel of opcode
  //   DON'T CHANGE THE LOCATIONS OF THE INPUTS AND OUTPUTS!
  //   OUTPUT from your circuit
  //   R-Type opcode=0x33->BSel=0
  //   B-Type opcode=0x63
  //   UJ-Type opcode=0x6f
  //   I-Type opcode=0x67
  //   The logic of PCSel
  //   The logic of ALUSel
endmodule
