// Logisim project cpu.circ as structural Verilog: 1 circuit, main circuit cpu
module cpu (
  input  clk,
  input  [31:0] INSTRUCTION,
  input  [31:0] READ_DATA,
  output [31:0] WRITE_ADDRESS,
  output [31:0] PROGRAM_COUNTER,
  output [31:0] ra,
  output [31:0] sp,
  output [31:0] t0,
  output [31:0] t1,
  output [31:0] t2,
  output [31:0] s0,
  output [31:0] s1,
  output [31:0] a0,
  output [31:0] tohost,
  output [3:0] WRITE_ENABLE,
  output [31:0] WRITE_DATA
);

  wire and_1_out, and_2_out, and_3_out, ASel, B_Type, BrEq, BrLt, BrUn, BSel, control_logic_1_regwen,
       I_Type1, I_Type2, I_Type3, I_Type4, IF_JUMP, MemRW, not_1_out, not_2_out, not_3_out, not_4_out,
       not_5_out, not_6_out, not_7_out, not_8_out, not_9_out, not_10_out, not_11_out, not_12_out, not_13_out,
       not_14_out, not_15_out, not_16_out, not_17_out, not_18_out, not_19_out, not_20_out, not_21_out,
       not_22_out, not_23_out, not_24_out, not_25_out, not_26_out, not_27_out, not_28_out, not_29_out,
       not_30_out, not_31_out, not_32_out, or_1_out, PCSel, R_Type, S_Type, U_Type1, U_Type2, UJ_Type;
  wire [1:0] WBSel;
  wire [2:0] control_logic_1_immsel, funct3;
  wire [3:0] ALUSel;
  wire [6:0] funct7;
  wire [24:0] inst_2s;
  wire [31:0] adder_1_out, adder_2_out, bit_extender_1_out, bit_extender_2_out, imm, multiplexer_1_out,
       multiplexer_3_out, multiplexer_4_out, multiplexer_5_out, multiplexer_6_out, pc_2s, READ_DATA_EXT,
       regfile_1_read_data_1;

  and and_1 (and_1_out, PCSel, not_1_out);
  Adder #(.width(32)) adder_1 (.a(PROGRAM_COUNTER), .b(32'h4), .out(adder_1_out));  // open: cin, cout
  Multiplexer #(.enable("false"), .width(32)) multiplexer_1 (
    .in0(adder_1_out), .in1(WRITE_ADDRESS), .out(multiplexer_1_out), .sel(and_1_out));
  not not_1 (not_1_out, IF_JUMP);
  Register #(.width(32)) register_1 (
    .D(INSTRUCTION), .en(1'b1), .clk(clk), .Q({funct7, inst_2s[24:15], funct3, inst_2s[11:0]}));  // open: clr
  Register #(.width(32)) PC (.D(multiplexer_1_out), .en(1'b1), .clk(clk), .Q(PROGRAM_COUNTER));  // open: clr
  Register #(.width(32)) register_2 (.D(PROGRAM_COUNTER), .en(1'b1), .clk(clk), .Q(pc_2s));  // open: clr
  control_logic control_logic_1 (
    .CSRWen(I_Type4), .PCSel(PCSel), .RegWEn(control_logic_1_regwen), .ImmSel(control_logic_1_immsel),
    .BrUn(BrUn), .ASel(ASel), .BSel(BSel), .ALUSel(ALUSel), .MemRW(MemRW), .WBSel(WBSel), .CSRSel(I_Type4),
    .inst({funct7, inst_2s[24:15], funct3, inst_2s[11:0]}), .BrEq(BrEq), .BrLt(BrLt));
  not not_2 (not_2_out, IF_JUMP);
  imm_gen imm_gen_1 (
    .inst({funct7, inst_2s[24:15], funct3, inst_2s[11:0]}), .ImmSel(control_logic_1_immsel), .imm(imm));
  and and_2 (and_2_out, control_logic_1_regwen, not_2_out);
  not not_3 (not_3_out, IF_JUMP);
  or or_1 (or_1_out, UJ_Type, PCSel, I_Type3);
  Register #(.width(1)) register_3 (.D(and_3_out), .clk(clk), .Q(IF_JUMP));  // open: en, clr
  and and_3 (and_3_out, not_3_out, or_1_out);
  regfile regfile_1 (
    .rs1(inst_2s[19:15]), .rs2(inst_2s[24:20]), .rd(inst_2s[11:7]), .Write_Data(multiplexer_6_out),
    .RegWEn(and_2_out), .clk(clk), .ra(ra), .sp(sp), .t0(t0), .t1(t1), .t2(t2), .s0(s0), .s1(s1), .a0(a0),
    .Read_Data_1(regfile_1_read_data_1), .Read_Data_2(WRITE_DATA));
  Multiplexer #(.enable("false"), .select(3), .width(4)) multiplexer_2 (
    .in0(4'b0001), .in1(4'b0011), .in2(4'b1111), .out(WRITE_ENABLE), .sel(funct3));  // open: in3, in4, in5, in6, in7
  branch_comp branch_comp_1 (.rs1(regfile_1_read_data_1), .rs2(WRITE_DATA), .BrUn(BrUn), .BrEq(BrEq), .BrLt(BrLt));
  Multiplexer #(.enable("false"), .width(32)) multiplexer_3 (
    .in0(regfile_1_read_data_1), .in1(imm), .out(multiplexer_3_out), .sel(funct3[2]));
  Multiplexer #(.enable("false"), .width(32)) multiplexer_4 (
    .in0(regfile_1_read_data_1), .in1(pc_2s), .out(multiplexer_4_out), .sel(ASel));
  Multiplexer #(.enable("false"), .width(32)) multiplexer_5 (
    .in0(WRITE_DATA), .in1(imm), .out(multiplexer_5_out), .sel(BSel));
  alu alu_1 (.Result(WRITE_ADDRESS), .A(multiplexer_4_out), .B(multiplexer_5_out), .ALUSel(ALUSel));
  csr csr_1 (
    .CSR_address({funct7, inst_2s[24:20]}), .CSR_din(multiplexer_3_out), .CSR_WE(I_Type4), .clk(clk),
    .tohost(tohost));
  Adder #(.width(32)) adder_2 (.a(pc_2s), .b(32'h4), .out(adder_2_out));  // open: cin, cout
  assign bit_extender_1_out = {{24{READ_DATA[7]}}, READ_DATA[7:0]};  // Bit_Extender bit_extender_1
  assign bit_extender_2_out = {{16{READ_DATA[15]}}, READ_DATA[15:0]};  // Bit_Extender bit_extender_2
  Multiplexer #(.enable("false"), .select(2), .width(32)) multiplexer_6 (
    .in0(READ_DATA_EXT), .in1(WRITE_ADDRESS), .in2(adder_2_out), .out(multiplexer_6_out), .sel(WBSel));  // open: in3
  Multiplexer #(.enable("false"), .select(3), .width(32)) multiplexer_7 (
    .in0(bit_extender_1_out), .in1(bit_extender_2_out), .in2(READ_DATA), .out(READ_DATA_EXT), .sel(funct3));  // open: in3, in4, in5, in6, in7
  not not_4 (not_4_out, inst_2s[2]);
  not not_5 (not_5_out, inst_2s[3]);
  not not_6 (not_6_out, inst_2s[6]);
  not not_7 (not_7_out, inst_2s[2]);
  not not_8 (not_8_out, inst_2s[3]);
  not not_9 (not_9_out, inst_2s[4]);
  not not_10 (not_10_out, inst_2s[2]);
  not not_11 (not_11_out, inst_2s[3]);
  not not_12 (not_12_out, inst_2s[4]);
  not not_13 (not_13_out, inst_2s[6]);
  not not_14 (not_14_out, inst_2s[2]);
  not not_15 (not_15_out, inst_2s[3]);
  not not_16 (not_16_out, inst_2s[4]);
  not not_17 (not_17_out, inst_2s[5]);
  not not_18 (not_18_out, inst_2s[6]);
  not not_19 (not_19_out, inst_2s[2]);
  not not_20 (not_20_out, inst_2s[3]);
  not not_21 (not_21_out, inst_2s[5]);
  not not_22 (not_22_out, inst_2s[6]);
  not not_23 (not_23_out, inst_2s[3]);
  not not_24 (not_24_out, inst_2s[4]);
  not not_25 (not_25_out, inst_2s[2]);
  not not_26 (not_26_out, inst_2s[3]);
  not not_27 (not_27_out, inst_2s[4]);
  not not_28 (not_28_out, inst_2s[3]);
  not not_29 (not_29_out, inst_2s[5]);
  not not_30 (not_30_out, inst_2s[6]);
  not not_31 (not_31_out, inst_2s[3]);
  not not_32 (not_32_out, inst_2s[6]);
  and and_4 (R_Type, inst_2s[0], inst_2s[1], not_4_out, not_5_out, inst_2s[4], inst_2s[5], not_6_out);
  and and_5 (B_Type, inst_2s[0], inst_2s[1], not_7_out, not_8_out, not_9_out, inst_2s[5], inst_2s[6]);
  and and_6 (S_Type, inst_2s[0], inst_2s[1], not_10_out, not_11_out, not_12_out, inst_2s[5], not_13_out);
  and and_7 (I_Type1, inst_2s[0], inst_2s[1], not_14_out, not_15_out, not_16_out, not_17_out, not_18_out);
  and and_8 (I_Type2, inst_2s[0], inst_2s[1], not_19_out, not_20_out, inst_2s[4], not_21_out, not_22_out);
  and and_9 (I_Type3, inst_2s[0], inst_2s[1], inst_2s[2], not_23_out, not_24_out, inst_2s[5], inst_2s[6]);
  and and_10 (I_Type4, inst_2s[0], inst_2s[1], not_25_out, not_26_out, inst_2s[4], inst_2s[5], inst_2s[6]);
  and and_11 (UJ_Type, inst_2s[0], inst_2s[1], inst_2s[2], inst_2s[3], not_27_out, inst_2s[5], inst_2s[6]);
  and and_12 (U_Type1, inst_2s[0], inst_2s[1], inst_2s[2], not_28_out, inst_2s[4], not_29_out, not_30_out);
  and and_13 (U_Type2, inst_2s[0], inst_2s[1], inst_2s[2], not_31_out, inst_2s[4], inst_2s[5], not_32_out);

  // Other names for the same wires on the sheet: rs2[4:0] = inst_2s[24:20]; inst_2s (some bits) = {funct7, funct3};
  //   opcode[6:0] = inst_2s[6:0]; rd[4:0] = inst_2s[11:7]; rs1[4:0] = inst_2s[19:15]

  // Notes on the sheet:
  //   Output to IMEM
  //   IMEM (do **NOT** move this)
  //   Inputs from IMEM
  //   Inputs/Outputs for testing. Do **NOT** move these.
  //   Outputs To DMEM
  //   DMEM (do **NOT** move this)
  //   Inputs From DMEM
  //   The tunnel of opcode
endmodule
