// Logisim project csr.circ as structural Verilog: 1 circuit, main circuit csr
module csr (
  input  [11:0] CSR_address,
  input  [31:0] CSR_din,
  input  CSR_WE,
  input  clk,
  output [31:0] tohost
);

  wire HEX51E, not_1_out, not_2_out, not_3_out, not_4_out, not_5_out, not_6_out;

  not not_1 (not_1_out, CSR_address[0]);
  not not_2 (not_2_out, CSR_address[5]);
  not not_3 (not_3_out, CSR_address[6]);
  not not_4 (not_4_out, CSR_address[7]);
  not not_5 (not_5_out, CSR_address[9]);
  not not_6 (not_6_out, CSR_address[11]);
  and and_1 (HEX51E, not_1_out, CSR_address[1], CSR_address[2], CSR_address[3], CSR_address[4], not_2_out, not_3_out, not_4_out, CSR_address[8], not_5_out, CSR_address[10], not_6_out);
  Register #(.width(32)) register_1 (.D(CSR_din), .en(HEX51E), .clk(clk), .Q(tohost));  // open: clr

  // Other names for the same wires on the sheet: address[11:0] = CSR_address; data[31:0] = CSR_din; WE = CSR_WE

  // Notes on the sheet:
  //   INPUTS to your circuit
  //   address=0x51E
  //   DON'T CHANGE THE LOCATIONS OF THE INPUTS AND OUTPUTS!
  //   OUTPUT from your circuit
endmodule
