// Logisim project imm_gen.circ as structural Verilog: 1 circuit, main circuit imm_gen
module imm_gen (
  input  [31:0] inst,
  input  [2:0] ImmSel,
  output [31:0] imm
);

  wire [31:0] immcsr;
  wire [31:11] immi, imms;
  wire [31:12] immsb;
  wire [31:20] immuj;

  assign immcsr = {{27{inst[19]}}, inst[19:15]};  // Bit_Extender bit_extender_1
  assign immi = {{20{inst[31]}}, inst[31]};  // Bit_Extender bit_extender_2
  assign imms = {{20{inst[31]}}, inst[31]};  // Bit_Extender bit_extender_3
  assign immsb = {{19{inst[31]}}, inst[31]};  // Bit_Extender bit_extender_4
  assign immuj = {{11{inst[31]}}, inst[31]};  // Bit_Extender bit_extender_5
  Multiplexer #(.enable("false"), .select(3), .width(32)) multiplexer_1 (
    .in0({immi, inst[30:20]}), .in1({imms, inst[30:25], inst[11:7]}),
    .in2({immsb, inst[7], inst[30:25], inst[11:8], 1'b0}),
    .in3({immuj, inst[19:12], inst[20], inst[30:21], 1'b0}), .in4({inst[31:12], {12{1'b0}}}), .in5(immcsr),
    .out(imm), .sel(ImmSel));  // open: in6, in7

  // Other names for the same wires on the sheet: imms[10:0] = {inst[30:25], inst[11:7]};
  //   immsb[11:1] = {inst[7], inst[30:25], inst[11:8]}; immu[31:12] = inst[31:12]; immi[10:0] = inst[30:20];
  //   immuj[19:1] = {inst[19:12], inst[20], inst[30:21]}

  // Notes on the sheet:
  //   INPUTS to your circuit
  //   DON'T CHANGE THE LOCATIONS OF THE INPUTS AND OUTPUTS!
  //   OUTPUT from your circuit
endmodule
