// Logisim project regfile.circ as structural Verilog: 1 circuit, main circuit regfile
module regfile (
  input  [4:0] rs1,
  input  [4:0] rs2,
  input  [4:0] rd,
  input  [31:0] Write_Data,
  input  RegWEn,
  input  clk,
  output [31:0] ra,
  output [31:0] sp,
  output [31:0] t0,
  output [31:0] t1,
  output [31:0] t2,
  output [31:0] s0,
  output [31:0] s1,
  output [31:0] a0,
  output [31:0] Read_Data_1,
  output [31:0] Read_Data_2
);

  wire clk_t, decoder_1_out0, decoder_1_out1, decoder_1_out2, decoder_1_out3, decoder_2_out0, decoder_2_out1,
       decoder_2_out2, decoder_2_out3, decoder_3_out0, decoder_3_out1, decoder_3_out2, decoder_3_out3,
       decoder_4_out0, decoder_4_out1, decoder_4_out2, decoder_4_out3, decoder_7_out0, decoder_7_out1,
       decoder_8_out0, decoder_8_out1, decoder_10_out0, decoder_10_out1, decoder_12_out0, decoder_12_out1,
       decoder_12_out2, decoder_12_out3, decoder_13_out0, decoder_13_out1, decoder_13_out2, decoder_13_out3,
       decoder_14_out0, decoder_14_out1, decoder_14_out2, decoder_14_out3, decoder_15_out0, decoder_15_out1,
       decoder_15_out2, decoder_15_out3, wt1, wt2, wt3, wt4, wt5, wt6, wt7, wt8;
  wire [31:0] multiplexer_1_out, multiplexer_2_out, multiplexer_3_out, multiplexer_4_out, multiplexer_5_out,
       multiplexer_6_out, multiplexer_7_out, multiplexer_8_out, multiplexer_11_out, multiplexer_12_out,
       multiplexer_13_out, multiplexer_14_out, multiplexer_15_out, multiplexer_16_out, multiplexer_17_out,
       multiplexer_18_out, multiplexer_19_out, multiplexer_20_out, multiplexer_21_out, multiplexer_22_out,
       multiplexer_23_out, multiplexer_24_out, multiplexer_25_out, multiplexer_26_out, multiplexer_27_out,
       multiplexer_28_out, multiplexer_29_out, multiplexer_30_out, multiplexer_31_out, multiplexer_32_out,
       multiplexer_33_out, multiplexer_34_out, multiplexer_35_out, multiplexer_36_out, multiplexer_37_out,
       multiplexer_38_out, multiplexer_39_out, multiplexer_40_out, multiplexer_41_out, x0, x3, x4, x11, x12,
       x13, x14, x15, x16, x17, x18, x19, x20, x21, x22, x23, x24, x25, x26, x27, x28, x29, x30, x31;

  Clock clock_1 (.out(clk_t));
  Multiplexer #(.enable("false"), .select(3), .width(32)) multiplexer_1 (
    .in0(x0), .in1(ra), .in2(sp), .in3(x3), .in4(x4), .in5(t0), .in6(t1), .in7(t2), .out(multiplexer_1_out),
    .sel(rs1[2:0]));
  Multiplexer #(.enable("false"), .select(3), .width(32)) multiplexer_2 (
    .in0(x16), .in1(x17), .in2(x18), .in3(x19), .in4(x20), .in5(x21), .in6(x22), .in7(x23),
    .out(multiplexer_2_out), .sel(rs1[2:0]));
  Multiplexer #(.enable("false"), .select(3), .width(32)) multiplexer_3 (
    .in0(x0), .in1(ra), .in2(sp), .in3(x3), .in4(x4), .in5(t0), .in6(t1), .in7(t2), .out(multiplexer_3_out),
    .sel(rs2[2:0]));
  Multiplexer #(.enable("false"), .select(3), .width(32)) multiplexer_4 (
    .in0(x16), .in1(x17), .in2(x18), .in3(x19), .in4(x20), .in5(x21), .in6(x22), .in7(x23),
    .out(multiplexer_4_out), .sel(rs2[2:0]));
  Multiplexer #(.enable("false"), .select(3), .width(32)) multiplexer_5 (
    .in0(s0), .in1(s1), .in2(a0), .in3(x11), .in4(x12), .in5(x13), .in6(x14), .in7(x15),
    .out(multiplexer_5_out), .sel(rs1[2:0]));
  Multiplexer #(.enable("false"), .select(3), .width(32)) multiplexer_6 (
    .in0(x24), .in1(x25), .in2(x26), .in3(x27), .in4(x28), .in5(x29), .in6(x30), .in7(x31),
    .out(multiplexer_6_out), .sel(rs1[2:0]));
  Multiplexer #(.enable("false"), .select(3), .width(32)) multiplexer_7 (
    .in0(s0), .in1(s1), .in2(a0), .in3(x11), .in4(x12), .in5(x13), .in6(x14), .in7(x15),
    .out(multiplexer_7_out), .sel(rs2[2:0]));
  Multiplexer #(.enable("false"), .select(3), .width(32)) multiplexer_8 (
    .in0(x24), .in1(x25), .in2(x26), .in3(x27), .in4(x28), .in5(x29), .in6(x30), .in7(x31),
    .out(multiplexer_8_out), .sel(rs2[2:0]));
  Multiplexer #(.enable("false"), .select(2), .width(32)) multiplexer_9 (
    .in0(multiplexer_1_out), .in1(multiplexer_5_out), .in2(multiplexer_2_out), .in3(multiplexer_6_out),
    .out(Read_Data_1), .sel(rs1[4:3]));
  Multiplexer #(.enable("false"), .select(2), .width(32)) multiplexer_10 (
    .in0(multiplexer_3_out), .in1(multiplexer_7_out), .in2(multiplexer_4_out), .in3(multiplexer_8_out),
    .out(Read_Data_2), .sel(rs2[4:3]));
  Register #(.width(32)) register_1 (.D({32{1'b0}}), .en(RegWEn), .clk(clk_t), .Q(x0));  // open: clr
  Multiplexer #(.enable("false"), .width(32)) multiplexer_11 (
    .in0(x4), .in1(Write_Data), .out(multiplexer_11_out), .sel(decoder_2_out0));
  Multiplexer #(.enable("false"), .width(32)) multiplexer_12 (
    .in0(s0), .in1(Write_Data), .out(multiplexer_12_out), .sel(decoder_3_out0));
  Multiplexer #(.enable("false"), .width(32)) multiplexer_13 (
    .in0(x12), .in1(Write_Data), .out(multiplexer_13_out), .sel(decoder_4_out0));
  Register #(.width(32)) register_2 (.D(multiplexer_11_out), .en(RegWEn), .clk(clk_t), .Q(x4));  // open: clr
  Register #(.width(32)) register_3 (.D(multiplexer_12_out), .en(RegWEn), .clk(clk_t), .Q(s0));  // open: clr
  Register #(.width(32)) register_4 (.D(multiplexer_13_out), .en(RegWEn), .clk(clk_t), .Q(ra));  // open: clr
  Multiplexer #(.enable("false"), .width(32)) multiplexer_14 (
    .in0(ra), .in1(Write_Data), .out(multiplexer_14_out), .sel(decoder_1_out1));
  Multiplexer #(.enable("false"), .width(32)) multiplexer_15 (
    .in0(t0), .in1(Write_Data), .out(multiplexer_15_out), .sel(decoder_2_out1));
  Multiplexer #(.enable("false"), .width(32)) multiplexer_16 (
    .in0(x13), .in1(Write_Data), .out(multiplexer_16_out), .sel(decoder_4_out1));
  Multiplexer #(.enable("false"), .width(32)) multiplexer_17 (
    .in0(s1), .in1(Write_Data), .out(multiplexer_17_out), .sel(decoder_3_out1));
  Register #(.width(32)) register_5 (.D(multiplexer_16_out), .en(RegWEn), .clk(clk_t), .Q(ra));  // open: clr
  Register #(.width(32)) register_6 (.D(multiplexer_14_out), .en(RegWEn), .clk(clk_t), .Q(ra));  // open: clr
  Decoder #(.select(2)) decoder_1 (
    .out0(decoder_1_out0), .out1(decoder_1_out1), .out2(decoder_1_out2), .out3(decoder_1_out3),
    .sel(rd[1:0]), .en(wt1));
  Register #(.width(32)) register_7 (.D(multiplexer_15_out), .en(RegWEn), .clk(clk_t), .Q(t0));  // open: clr
  Decoder #(.select(2)) decoder_2 (
    .out0(decoder_2_out0), .out1(decoder_2_out1), .out2(decoder_2_out2), .out3(decoder_2_out3),
    .sel(rd[1:0]), .en(wt2));
  Register #(.width(32)) register_8 (.D(multiplexer_17_out), .en(RegWEn), .clk(clk_t), .Q(s1));  // open: clr
  Decoder #(.select(2)) decoder_3 (
    .out0(decoder_3_out0), .out1(decoder_3_out1), .out2(decoder_3_out2), .out3(decoder_3_out3),
    .sel(rd[1:0]), .en(wt3));
  Decoder #(.select(2)) decoder_4 (
    .out0(decoder_4_out0), .out1(decoder_4_out1), .out2(decoder_4_out2), .out3(decoder_4_out3),
    .sel(rd[1:0]), .en(wt4));
  Multiplexer #(.enable("false"), .width(32)) multiplexer_18 (
    .in0(sp), .in1(Write_Data), .out(multiplexer_18_out), .sel(decoder_1_out2));
  Multiplexer #(.enable("false"), .width(32)) multiplexer_19 (
    .in0(t1), .in1(Write_Data), .out(multiplexer_19_out), .sel(decoder_2_out2));
  Multiplexer #(.enable("false"), .width(32)) multiplexer_20 (
    .in0(a0), .in1(Write_Data), .out(multiplexer_20_out), .sel(decoder_3_out2));
  Multiplexer #(.enable("false"), .width(32)) multiplexer_21 (
    .in0(x14), .in1(Write_Data), .out(multiplexer_21_out), .sel(decoder_4_out2));
  Decoder decoder_5 (.out0(wt1), .out1(wt2), .sel(rd[2]), .en(decoder_7_out0));
  Register #(.width(32)) register_9 (.D(multiplexer_18_out), .en(RegWEn), .clk(clk_t), .Q(sp));  // open: clr
  Register #(.width(32)) register_10 (.D(multiplexer_19_out), .en(RegWEn), .clk(clk_t), .Q(t1));  // open: clr
  Register #(.width(32)) register_11 (.D(multiplexer_20_out), .en(RegWEn), .clk(clk_t), .Q(a0));  // open: clr
  Register #(.width(32)) register_12 (.D(multiplexer_21_out), .en(RegWEn), .clk(clk_t), .Q(ra));  // open: clr
  Decoder decoder_6 (.out0(wt3), .out1(wt4), .sel(rd[2]), .en(decoder_7_out1));
  Decoder decoder_7 (.out0(decoder_7_out0), .out1(decoder_7_out1), .sel(rd[3]), .en(decoder_8_out0));
  Decoder #(.enable("false")) decoder_8 (.out0(decoder_8_out0), .out1(decoder_8_out1), .sel(rd[4]));
  Multiplexer #(.enable("false"), .width(32)) multiplexer_22 (
    .in0(x3), .in1(Write_Data), .out(multiplexer_22_out), .sel(decoder_1_out3));
  Multiplexer #(.enable("false"), .width(32)) multiplexer_23 (
    .in0(t2), .in1(Write_Data), .out(multiplexer_23_out), .sel(decoder_2_out3));
  Multiplexer #(.enable("false"), .width(32)) multiplexer_24 (
    .in0(x11), .in1(Write_Data), .out(multiplexer_24_out), .sel(decoder_3_out3));
  Multiplexer #(.enable("false"), .width(32)) multiplexer_25 (
    .in0(x15), .in1(Write_Data), .out(multiplexer_25_out), .sel(decoder_4_out3));
  Register #(.width(32)) register_13 (.D(multiplexer_22_out), .en(RegWEn), .clk(clk_t), .Q(x3));  // open: clr
  Register #(.width(32)) register_14 (.D(multiplexer_23_out), .en(RegWEn), .clk(clk_t), .Q(t2));  // open: clr
  Register #(.width(32)) register_15 (.D(multiplexer_24_out), .en(RegWEn), .clk(clk_t), .Q(x11));  // open: clr
  Register #(.width(32)) register_16 (.D(multiplexer_25_out), .en(RegWEn), .clk(clk_t), .Q(ra));  // open: clr
  Decoder decoder_9 (.out0(wt5), .out1(wt6), .sel(rd[2]), .en(decoder_10_out0));
  Decoder decoder_10 (.out0(decoder_10_out0), .out1(decoder_10_out1), .sel(rd[3]), .en(decoder_8_out1));
  Decoder decoder_11 (.out0(wt7), .out1(wt8), .sel(rd[2]), .en(decoder_10_out1));
  Multiplexer #(.enable("false"), .width(32)) multiplexer_26 (
    .in0(x16), .in1(Write_Data), .out(multiplexer_26_out), .sel(decoder_12_out0));
  Multiplexer #(.enable("false"), .width(32)) multiplexer_27 (
    .in0(x20), .in1(Write_Data), .out(multiplexer_27_out), .sel(decoder_13_out0));
  Multiplexer #(.enable("false"), .width(32)) multiplexer_28 (
    .in0(x24), .in1(Write_Data), .out(multiplexer_28_out), .sel(decoder_14_out0));
  Register #(.width(32)) register_17 (.D(multiplexer_28_out), .en(RegWEn), .clk(clk_t), .Q(x24));  // open: clr
  Multiplexer #(.enable("false"), .width(32)) multiplexer_29 (
    .in0(x28), .in1(Write_Data), .out(multiplexer_29_out), .sel(decoder_15_out0));
  Register #(.width(32)) register_18 (.D(multiplexer_26_out), .en(RegWEn), .clk(clk_t), .Q(x16));  // open: clr
  Register #(.width(32)) register_19 (.D(multiplexer_27_out), .en(RegWEn), .clk(clk_t), .Q(x20));  // open: clr
  Register #(.width(32)) register_20 (.D(multiplexer_29_out), .en(RegWEn), .clk(clk_t), .Q(x28));  // open: clr
  Multiplexer #(.enable("false"), .width(32)) multiplexer_30 (
    .in0(x17), .in1(Write_Data), .out(multiplexer_30_out), .sel(decoder_12_out1));
  Multiplexer #(.enable("false"), .width(32)) multiplexer_31 (
    .in0(x21), .in1(Write_Data), .out(multiplexer_31_out), .sel(decoder_13_out1));
  Multiplexer #(.enable("false"), .width(32)) multiplexer_32 (
    .in0(x25), .in1(Write_Data), .out(multiplexer_32_out), .sel(decoder_14_out1));
  Register #(.width(32)) register_21 (.D(multiplexer_30_out), .en(RegWEn), .clk(clk_t), .Q(x17));  // open: clr
  Register #(.width(32)) register_22 (.D(multiplexer_31_out), .en(RegWEn), .clk(clk_t), .Q(x21));  // open: clr
  Register #(.width(32)) register_23 (.D(multiplexer_32_out), .en(RegWEn), .clk(clk_t), .Q(x25));  // open: clr
  Multiplexer #(.enable("false"), .width(32)) multiplexer_33 (
    .in0(x29), .in1(Write_Data), .out(multiplexer_33_out), .sel(decoder_15_out1));
  Decoder #(.select(2)) decoder_12 (
    .out0(decoder_12_out0), .out1(decoder_12_out1), .out2(decoder_12_out2), .out3(decoder_12_out3),
    .sel(rd[1:0]), .en(wt5));
  Decoder #(.select(2)) decoder_13 (
    .out0(decoder_13_out0), .out1(decoder_13_out1), .out2(decoder_13_out2), .out3(decoder_13_out3),
    .sel(rd[1:0]), .en(wt6));
  Decoder #(.select(2)) decoder_14 (
    .out0(decoder_14_out0), .out1(decoder_14_out1), .out2(decoder_14_out2), .out3(decoder_14_out3),
    .sel(rd[1:0]), .en(wt7));
  Register #(.width(32)) register_24 (.D(multiplexer_33_out), .en(RegWEn), .clk(clk_t), .Q(x29));  // open: clr
  Decoder #(.select(2)) decoder_15 (
    .out0(decoder_15_out0), .out1(decoder_15_out1), .out2(decoder_15_out2), .out3(decoder_15_out3),
    .sel(rd[1:0]), .en(wt8));
  Multiplexer #(.enable("false"), .width(32)) multiplexer_34 (
    .in0(x18), .in1(Write_Data), .out(multiplexer_34_out), .sel(decoder_12_out2));
  Multiplexer #(.enable("false"), .width(32)) multiplexer_35 (
    .in0(x22), .in1(Write_Data), .out(multiplexer_35_out), .sel(decoder_13_out2));
  Multiplexer #(.enable("false"), .width(32)) multiplexer_36 (
    .in0(x26), .in1(Write_Data), .out(multiplexer_36_out), .sel(decoder_14_out2));
  Multiplexer #(.enable("false"), .width(32)) multiplexer_37 (
    .in0(x30), .in1(Write_Data), .out(multiplexer_37_out), .sel(decoder_15_out2));
  Register #(.width(32)) register_25 (.D(multiplexer_34_out), .en(RegWEn), .clk(clk_t), .Q(x18));  // open: clr
  Multiplexer #(.enable("false"), .width(32)) multiplexer_38 (
    .in0(x19), .in1(Write_Data), .out(multiplexer_38_out), .sel(decoder_12_out3));
  Register #(.width(32)) register_26 (.D(multiplexer_35_out), .en(RegWEn), .clk(clk_t), .Q(x22));  // open: clr
  Multiplexer #(.enable("false"), .width(32)) multiplexer_39 (
    .in0(x23), .in1(Write_Data), .out(multiplexer_39_out), .sel(decoder_13_out3));
  Register #(.width(32)) register_27 (.D(multiplexer_36_out), .en(RegWEn), .clk(clk_t), .Q(x26));  // open: clr
  Register #(.width(32)) register_28 (.D(multiplexer_37_out), .en(RegWEn), .clk(clk_t), .Q(x30));  // open: clr
  Multiplexer #(.enable("false"), .width(32)) multiplexer_40 (
    .in0(x27), .in1(Write_Data), .out(multiplexer_40_out), .sel(decoder_14_out3));
  Multiplexer #(.enable("false"), .width(32)) multiplexer_41 (
    .in0(x31), .in1(Write_Data), .out(multiplexer_41_out), .sel(decoder_15_out3));
  Register #(.width(32)) register_29 (.D(multiplexer_38_out), .en(RegWEn), .clk(clk_t), .Q(x19));  // open: clr
  Register #(.width(32)) register_30 (.D(multiplexer_39_out), .en(RegWEn), .clk(clk_t), .Q(x23));  // open: clr
  Register #(.width(32)) register_31 (.D(multiplexer_40_out), .en(RegWEn), .clk(clk_t), .Q(x27));  // open: clr
  Register #(.width(32)) register_32 (.D(multiplexer_41_out), .en(RegWEn), .clk(clk_t), .Q(x31));  // open: clr

  // Other names for the same wires on the sheet: read_data1[31:0] = Read_Data_1; read_data2[31:0] = Read_Data_2;
  //   read_reg1[4:0] = rs1; rreg1_012[2:0] = rs1[2:0]; rreg1_34[1:0] = rs1[4:3]; read_reg2[4:0] = rs2;
  //   rreg2_012[2:0] = rs2[2:0]; rreg2_34[1:0] = rs2[4:3]; write_en = RegWEn; wr01[1:0] = rd[1:0];
  //   write_reg[4:0] = rd; wr2 = rd[2]; wr3 = rd[3]; wr4 = rd[4]; x1[31:0] = ra; x2[31:0] = sp; x5[31:0] = t0;
  //   x6[31:0] = t1; x7[31:0] = t2; x8[31:0] = s0; x9[31:0] = s1; x10[31:0] = a0

  // Notes on the sheet:
  //   INPUTS to your circuit
  //   DON'T CHANGE THE LOCATIONS OF THE INPUTS AND OUTPUTS!
  //   These are DEBUG/TEST outputs from your circuit.
  //   OUTPUTS from your circuit
endmodule
